// Digital circuit Semaforo.dig as structural Verilog
module Semaforo (
  input  P,
  input  CLK
);

  wire and_1_out, and_2_out, D0_q, D1_q, not_1_out, or_1_out, xor_1_out;

  not not_1 (not_1_out, D0_q);
  and and_1 (and_1_out, not_1_out, D1_q);
  and and_2 (and_2_out, not_1_out, P);
  xor xor_1 (xor_1_out, D1_q, D0_q);
  or or_1 (or_1_out, and_1_out, and_2_out);
  FlipFlopD D1 (.CLK(CLK), .D(xor_1_out), .Q(D1_q));
  FlipFlopD D0 (.CLK(CLK), .D(or_1_out), .Q(D0_q));
  LED LP2 ();  // open: in
  LED LP1 ();  // open: in
  LED LP0 ();  // open: in
  LED LS2 ();  // open: in
  LED LS1 ();  // open: in
  LED LS0 ();  // open: in
endmodule
